// Logisim project Pamiec-rejestrowa-5x8bit.circ as structural Verilog: 2 circuits, main circuit main
module main (
  input  SHIFT,
  input  D7,
  input  D6,
  input  D5,
  input  D4,
  input  D3,
  input  D2,
  input  D1,
  input  D0,
  input  D7_2,
  input  D6_2,
  input  D5_2,
  input  D4_2,
  input  D3_2,
  input  D2_2,
  input  D1_2,
  input  D0_2,
  input  D,
  input  D_2,
  output Q,
  output Q7,
  output Q6,
  output Q5,
  output Q4,
  output Q3,
  output Q2,
  output Q1,
  output Q0,
  output Q_2,
  output Q7_2,
  output Q6_2,
  output Q5_2,
  output Q4_2,
  output Q3_2,
  output Q2_2,
  output Q1_2,
  output Q0_2
);

  wire and_1_out, and_2_out, and_3_out, and_4_out, and_5_out, and_6_out, and_7_out, and_8_out, and_9_out,
       and_10_out, and_11_out, and_12_out, and_13_out, and_14_out, clock_1_out, clock_2_out, clock_3_out,
       clock_4_out, d_ff_1_q, d_ff_3_q, d_ff_5_q, d_ff_7_q, d_ff_10_q, d_ff_12_q, d_ff_14_q, d_ff_16_q,
       d_ff_18_q, d_ff_21_q, d_ff_23_q, d_ff_25_q, d_ff_30_q, d_ff_31_q, not_1_out, or_1_out, or_2_out,
       or_3_out, or_4_out, or_5_out, or_6_out, or_7_out;

  Clock clock_1 (.out(clock_1_out));
  Clock clock_2 (.out(clock_2_out));
  Clock clock_3 (.out(clock_3_out));
  Clock clock_4 (.out(clock_4_out));
  D_Flip_Flop d_ff_1 (.clk(clock_1_out), .D(D7), .Q(d_ff_1_q));  // open: Qn, preset, en, reset
  not not_1 (not_1_out, SHIFT);
  and and_1 (and_1_out, d_ff_1_q, SHIFT);
  and and_2 (and_2_out, not_1_out, D6);
  D_Flip_Flop d_ff_2 (.clk(clock_2_out), .D(D7_2), .Q(Q7));  // open: Qn, preset, en, reset
  D_Flip_Flop d_ff_3 (.clk(clock_3_out), .D(D), .Q(d_ff_3_q));  // open: Qn, preset, en, reset
  D_Flip_Flop d_ff_4 (.clk(clock_4_out), .D(D_2), .Q(Q7_2));  // open: Qn, preset, en, reset
  or or_1 (or_1_out, and_1_out, and_2_out);
  D_Flip_Flop d_ff_5 (.clk(clock_1_out), .D(or_1_out), .Q(d_ff_5_q));  // open: Qn, preset, en, reset
  D_Flip_Flop d_ff_6 (.clk(clock_2_out), .D(D6_2), .Q(Q6));  // open: Qn, preset, en, reset
  D_Flip_Flop d_ff_7 (.clk(clock_3_out), .D(d_ff_3_q), .Q(d_ff_7_q));  // open: Qn, preset, en, reset
  D_Flip_Flop d_ff_8 (.clk(clock_4_out), .D(Q7_2), .Q(Q6_2));  // open: Qn, preset, en, reset
  and and_3 (and_3_out, d_ff_5_q, SHIFT);
  and and_4 (and_4_out, not_1_out, D5);
  D_Flip_Flop d_ff_9 (.clk(clock_2_out), .D(D5_2), .Q(Q5));  // open: Qn, preset, en, reset
  D_Flip_Flop d_ff_10 (.clk(clock_3_out), .D(d_ff_7_q), .Q(d_ff_10_q));  // open: Qn, preset, en, reset
  D_Flip_Flop d_ff_11 (.clk(clock_4_out), .D(Q6_2), .Q(Q5_2));  // open: Qn, preset, en, reset
  or or_2 (or_2_out, and_3_out, and_4_out);
  D_Flip_Flop d_ff_12 (.clk(clock_1_out), .D(or_2_out), .Q(d_ff_12_q));  // open: Qn, preset, en, reset
  D_Flip_Flop d_ff_13 (.clk(clock_2_out), .D(D4_2), .Q(Q4));  // open: Qn, preset, en, reset
  D_Flip_Flop d_ff_14 (.clk(clock_3_out), .D(d_ff_10_q), .Q(d_ff_14_q));  // open: Qn, preset, en, reset
  D_Flip_Flop d_ff_15 (.clk(clock_4_out), .D(Q5_2), .Q(Q4_2));  // open: Qn, preset, en, reset
  and and_5 (and_5_out, d_ff_12_q, SHIFT);
  and and_6 (and_6_out, not_1_out, D4);
  D_Flip_Flop d_ff_16 (.clk(clock_1_out), .D(or_3_out), .Q(d_ff_16_q));  // open: Qn, preset, en, reset
  or or_3 (or_3_out, and_5_out, and_6_out);
  D_Flip_Flop d_ff_17 (.clk(clock_2_out), .D(D3_2), .Q(Q3));  // open: Qn, preset, en, reset
  D_Flip_Flop d_ff_18 (.clk(clock_3_out), .D(d_ff_14_q), .Q(d_ff_18_q));  // open: Qn, preset, en, reset
  D_Flip_Flop d_ff_19 (.clk(clock_4_out), .D(Q4_2), .Q(Q3_2));  // open: Qn, preset, en, reset
  D_Flip_Flop d_ff_20 (.clk(clock_2_out), .D(D2_2), .Q(Q2));  // open: Qn, preset, en, reset
  D_Flip_Flop d_ff_21 (.clk(clock_3_out), .D(d_ff_18_q), .Q(d_ff_21_q));  // open: Qn, preset, en, reset
  D_Flip_Flop d_ff_22 (.clk(clock_4_out), .D(Q3_2), .Q(Q2_2));  // open: Qn, preset, en, reset
  and and_7 (and_7_out, d_ff_16_q, SHIFT);
  and and_8 (and_8_out, not_1_out, D3);
  D_Flip_Flop d_ff_23 (.clk(clock_1_out), .D(or_4_out), .Q(d_ff_23_q));  // open: Qn, preset, en, reset
  or or_4 (or_4_out, and_7_out, and_8_out);
  D_Flip_Flop d_ff_24 (.clk(clock_2_out), .D(D1_2), .Q(Q1));  // open: Qn, preset, en, reset
  D_Flip_Flop d_ff_25 (.clk(clock_3_out), .D(d_ff_21_q), .Q(d_ff_25_q));  // open: Qn, preset, en, reset
  D_Flip_Flop d_ff_26 (.clk(clock_4_out), .D(Q2_2), .Q(Q1_2));  // open: Qn, preset, en, reset
  and and_9 (and_9_out, d_ff_23_q, SHIFT);
  D_Flip_Flop d_ff_27 (.clk(clock_2_out), .D(D0_2), .Q(Q0));  // open: Qn, preset, en, reset
  D_Flip_Flop d_ff_28 (.clk(clock_3_out), .D(d_ff_25_q), .Q(Q_2));  // open: Qn, preset, en, reset
  D_Flip_Flop d_ff_29 (.clk(clock_4_out), .D(Q1_2), .Q(Q0_2));  // open: Qn, preset, en, reset
  or or_5 (or_5_out, and_9_out, and_10_out);
  and and_10 (and_10_out, not_1_out, D2);
  D_Flip_Flop d_ff_30 (.clk(clock_1_out), .D(or_5_out), .Q(d_ff_30_q));  // open: Qn, preset, en, reset
  and and_11 (and_11_out, d_ff_30_q, SHIFT);
  and and_12 (and_12_out, not_1_out, D1);
  or or_6 (or_6_out, and_11_out, and_12_out);
  D_Flip_Flop d_ff_31 (.clk(clock_1_out), .D(or_6_out), .Q(d_ff_31_q));  // open: Qn, preset, en, reset
  and and_13 (and_13_out, d_ff_31_q, SHIFT);
  or or_7 (or_7_out, and_13_out, and_14_out);
  and and_14 (and_14_out, not_1_out, D0);
  D_Flip_Flop d_ff_32 (.clk(clock_1_out), .D(or_7_out), .Q(Q));  // open: Qn, preset, en, reset

  // Notes on the sheet:
  //   Rejestr równoległo-szeregowy
  //   Rejestr równoległo-równoległy
  //   Rejestr szeregowo-szeregowy
  //   Rejestr szeregowo-równoległy
endmodule

module rejestr (
  input  D7,
  input  D6,
  input  D5,
  input  D4,
  input  D3,
  input  D2,
  input  D1,
  input  D0,
  input  WE,
  input  A2,
  input  A1,
  input  A0,
  output out_13,
  output out_14,
  output out_15,
  output out_16,
  output out_17,
  output out_18,
  output out_19,
  output out_20
);

  wire and_1_out, and_2_out, and_3_out, and_4_out, and_5_out, and_6_out, and_7_out, and_8_out, and_9_out,
       and_10_out, and_11_out, and_12_out, and_13_out, and_14_out, and_15_out, and_16_out, and_17_out,
       and_18_out, and_19_out, and_20_out, and_21_out, and_22_out, and_23_out, and_24_out, and_25_out,
       and_26_out, and_27_out, and_28_out, and_29_out, and_30_out, and_31_out, and_32_out, and_33_out,
       and_34_out, and_35_out, and_36_out, and_37_out, and_38_out, and_39_out, and_40_out, and_41_out,
       and_42_out, and_43_out, and_44_out, and_45_out, and_46_out, and_47_out, and_48_out, and_49_out,
       and_50_out, d_ff_1_q, d_ff_2_q, d_ff_3_q, d_ff_4_q, d_ff_5_q, d_ff_6_q, d_ff_7_q, d_ff_8_q, d_ff_9_q,
       d_ff_10_q, d_ff_11_q, d_ff_12_q, d_ff_13_q, d_ff_14_q, d_ff_15_q, d_ff_16_q, d_ff_17_q, d_ff_18_q,
       d_ff_19_q, d_ff_20_q, d_ff_21_q, d_ff_22_q, d_ff_23_q, d_ff_24_q, d_ff_25_q, d_ff_26_q, d_ff_27_q,
       d_ff_28_q, d_ff_29_q, d_ff_30_q, d_ff_31_q, d_ff_32_q, d_ff_33_q, d_ff_34_q, d_ff_35_q, d_ff_36_q,
       d_ff_37_q, d_ff_38_q, d_ff_39_q, d_ff_40_q, not_1_out, not_2_out, not_3_out;

  not not_1 (not_1_out, A2);
  not not_2 (not_2_out, A1);
  not not_3 (not_3_out, A0);
  and and_1 (and_1_out, A2, not_2_out, not_3_out);
  and and_2 (and_2_out, not_1_out, A1, A0);
  and and_3 (and_3_out, not_1_out, A1, not_3_out);
  and and_4 (and_4_out, not_1_out, not_2_out, A0);
  and and_5 (and_5_out, not_1_out, not_2_out, not_3_out);
  and and_6 (and_6_out, WE, and_1_out);
  and and_7 (and_7_out, WE, and_2_out);
  and and_8 (and_8_out, WE, and_3_out);
  and and_9 (and_9_out, WE, and_4_out);
  and and_10 (and_10_out, WE, and_5_out);
  D_Flip_Flop d_ff_1 (.clk(and_6_out), .D(D0), .Q(d_ff_1_q));  // open: Qn, preset, en, reset
  D_Flip_Flop d_ff_2 (.clk(and_7_out), .D(D0), .Q(d_ff_2_q));  // open: Qn, preset, en, reset
  D_Flip_Flop d_ff_3 (.clk(and_8_out), .D(D0), .Q(d_ff_3_q));  // open: Qn, preset, en, reset
  D_Flip_Flop d_ff_4 (.clk(and_9_out), .D(D0), .Q(d_ff_4_q));  // open: Qn, preset, en, reset
  D_Flip_Flop d_ff_5 (.clk(and_10_out), .D(D0), .Q(d_ff_5_q));  // open: Qn, preset, en, reset
  D_Flip_Flop d_ff_6 (.clk(and_6_out), .D(D1), .Q(d_ff_6_q));  // open: Qn, preset, en, reset
  D_Flip_Flop d_ff_7 (.clk(and_7_out), .D(D1), .Q(d_ff_7_q));  // open: Qn, preset, en, reset
  D_Flip_Flop d_ff_8 (.clk(and_8_out), .D(D1), .Q(d_ff_8_q));  // open: Qn, preset, en, reset
  D_Flip_Flop d_ff_9 (.clk(and_9_out), .D(D1), .Q(d_ff_9_q));  // open: Qn, preset, en, reset
  D_Flip_Flop d_ff_10 (.clk(and_10_out), .D(D1), .Q(d_ff_10_q));  // open: Qn, preset, en, reset
  D_Flip_Flop d_ff_11 (.clk(and_6_out), .D(D2), .Q(d_ff_11_q));  // open: Qn, preset, en, reset
  D_Flip_Flop d_ff_12 (.clk(and_7_out), .D(D2), .Q(d_ff_12_q));  // open: Qn, preset, en, reset
  D_Flip_Flop d_ff_13 (.clk(and_8_out), .D(D2), .Q(d_ff_13_q));  // open: Qn, preset, en, reset
  D_Flip_Flop d_ff_14 (.clk(and_9_out), .D(D2), .Q(d_ff_14_q));  // open: Qn, preset, en, reset
  D_Flip_Flop d_ff_15 (.clk(and_10_out), .D(D2), .Q(d_ff_15_q));  // open: Qn, preset, en, reset
  D_Flip_Flop d_ff_16 (.clk(and_6_out), .D(D3), .Q(d_ff_16_q));  // open: Qn, preset, en, reset
  D_Flip_Flop d_ff_17 (.clk(and_7_out), .D(D3), .Q(d_ff_17_q));  // open: Qn, preset, en, reset
  D_Flip_Flop d_ff_18 (.clk(and_8_out), .D(D3), .Q(d_ff_18_q));  // open: Qn, preset, en, reset
  D_Flip_Flop d_ff_19 (.clk(and_9_out), .D(D3), .Q(d_ff_19_q));  // open: Qn, preset, en, reset
  D_Flip_Flop d_ff_20 (.clk(and_10_out), .D(D3), .Q(d_ff_20_q));  // open: Qn, preset, en, reset
  D_Flip_Flop d_ff_21 (.clk(and_6_out), .D(D4), .Q(d_ff_21_q));  // open: Qn, preset, en, reset
  D_Flip_Flop d_ff_22 (.clk(and_7_out), .D(D4), .Q(d_ff_22_q));  // open: Qn, preset, en, reset
  D_Flip_Flop d_ff_23 (.clk(and_8_out), .D(D4), .Q(d_ff_23_q));  // open: Qn, preset, en, reset
  D_Flip_Flop d_ff_24 (.clk(and_9_out), .D(D4), .Q(d_ff_24_q));  // open: Qn, preset, en, reset
  D_Flip_Flop d_ff_25 (.clk(and_10_out), .D(D4), .Q(d_ff_25_q));  // open: Qn, preset, en, reset
  D_Flip_Flop d_ff_26 (.clk(and_6_out), .D(D5), .Q(d_ff_26_q));  // open: Qn, preset, en, reset
  D_Flip_Flop d_ff_27 (.clk(and_7_out), .D(D5), .Q(d_ff_27_q));  // open: Qn, preset, en, reset
  D_Flip_Flop d_ff_28 (.clk(and_8_out), .D(D5), .Q(d_ff_28_q));  // open: Qn, preset, en, reset
  D_Flip_Flop d_ff_29 (.clk(and_9_out), .D(D5), .Q(d_ff_29_q));  // open: Qn, preset, en, reset
  D_Flip_Flop d_ff_30 (.clk(and_10_out), .D(D5), .Q(d_ff_30_q));  // open: Qn, preset, en, reset
  D_Flip_Flop d_ff_31 (.clk(and_6_out), .D(D6), .Q(d_ff_31_q));  // open: Qn, preset, en, reset
  D_Flip_Flop d_ff_32 (.clk(and_7_out), .D(D6), .Q(d_ff_32_q));  // open: Qn, preset, en, reset
  D_Flip_Flop d_ff_33 (.clk(and_8_out), .D(D6), .Q(d_ff_33_q));  // open: Qn, preset, en, reset
  D_Flip_Flop d_ff_34 (.clk(and_9_out), .D(D6), .Q(d_ff_34_q));  // open: Qn, preset, en, reset
  D_Flip_Flop d_ff_35 (.clk(and_10_out), .D(D6), .Q(d_ff_35_q));  // open: Qn, preset, en, reset
  D_Flip_Flop d_ff_36 (.clk(and_6_out), .D(D7), .Q(d_ff_36_q));  // open: Qn, preset, en, reset
  D_Flip_Flop d_ff_37 (.clk(and_7_out), .D(D7), .Q(d_ff_37_q));  // open: Qn, preset, en, reset
  D_Flip_Flop d_ff_38 (.clk(and_8_out), .D(D7), .Q(d_ff_38_q));  // open: Qn, preset, en, reset
  D_Flip_Flop d_ff_39 (.clk(and_9_out), .D(D7), .Q(d_ff_39_q));  // open: Qn, preset, en, reset
  D_Flip_Flop d_ff_40 (.clk(and_10_out), .D(D7), .Q(d_ff_40_q));  // open: Qn, preset, en, reset
  and and_11 (and_11_out, d_ff_36_q, and_1_out);
  and and_12 (and_12_out, d_ff_37_q, and_2_out);
  and and_13 (and_13_out, d_ff_38_q, and_3_out);
  and and_14 (and_14_out, d_ff_39_q, and_4_out);
  and and_15 (and_15_out, d_ff_40_q, and_5_out);
  and and_16 (and_16_out, d_ff_31_q, and_1_out);
  and and_17 (and_17_out, d_ff_32_q, and_2_out);
  and and_18 (and_18_out, d_ff_33_q, and_3_out);
  and and_19 (and_19_out, d_ff_34_q, and_4_out);
  and and_20 (and_20_out, d_ff_35_q, and_5_out);
  and and_21 (and_21_out, d_ff_26_q, and_1_out);
  and and_22 (and_22_out, d_ff_27_q, and_2_out);
  and and_23 (and_23_out, d_ff_28_q, and_3_out);
  and and_24 (and_24_out, d_ff_29_q, and_4_out);
  and and_25 (and_25_out, d_ff_30_q, and_5_out);
  and and_26 (and_26_out, d_ff_21_q, and_1_out);
  and and_27 (and_27_out, d_ff_22_q, and_2_out);
  and and_28 (and_28_out, d_ff_23_q, and_3_out);
  and and_29 (and_29_out, d_ff_24_q, and_4_out);
  and and_30 (and_30_out, d_ff_25_q, and_5_out);
  and and_31 (and_31_out, d_ff_16_q, and_1_out);
  and and_32 (and_32_out, d_ff_17_q, and_2_out);
  and and_33 (and_33_out, d_ff_18_q, and_3_out);
  and and_34 (and_34_out, d_ff_19_q, and_4_out);
  and and_35 (and_35_out, d_ff_20_q, and_5_out);
  and and_36 (and_36_out, d_ff_11_q, and_1_out);
  and and_37 (and_37_out, d_ff_12_q, and_2_out);
  and and_38 (and_38_out, d_ff_13_q, and_3_out);
  and and_39 (and_39_out, d_ff_14_q, and_4_out);
  and and_40 (and_40_out, d_ff_15_q, and_5_out);
  and and_41 (and_41_out, d_ff_6_q, and_1_out);
  and and_42 (and_42_out, d_ff_7_q, and_2_out);
  and and_43 (and_43_out, d_ff_8_q, and_3_out);
  and and_44 (and_44_out, d_ff_9_q, and_4_out);
  and and_45 (and_45_out, d_ff_10_q, and_5_out);
  and and_46 (and_46_out, d_ff_1_q, and_1_out);
  and and_47 (and_47_out, d_ff_2_q, and_2_out);
  and and_48 (and_48_out, d_ff_3_q, and_3_out);
  and and_49 (and_49_out, d_ff_4_q, and_4_out);
  and and_50 (and_50_out, d_ff_5_q, and_5_out);
  or or_1 (out_13, and_11_out, and_12_out, and_13_out, and_14_out, and_15_out);
  or or_2 (out_14, and_16_out, and_17_out, and_18_out, and_19_out, and_20_out);
  or or_3 (out_15, and_21_out, and_22_out, and_23_out, and_24_out, and_25_out);
  or or_4 (out_16, and_26_out, and_27_out, and_28_out, and_29_out, and_30_out);
  or or_5 (out_17, and_31_out, and_32_out, and_33_out, and_34_out, and_35_out);
  or or_6 (out_18, and_36_out, and_37_out, and_38_out, and_39_out, and_40_out);
  or or_7 (out_19, and_41_out, and_42_out, and_43_out, and_44_out, and_45_out);
  or or_8 (out_20, and_46_out, and_47_out, and_48_out, and_49_out, and_50_out);
endmodule
